# Fritzing sketch skisse (saved by Fritzing 0.8.3b)
breadboards: 2

parts:
  Part1 = Arduino Uno (Rev3)
  U1 = MAX7219 [package=dil24]
  R1 = Resistor [tolerance=±5% resistance=220 package=THT]
  R2 = Resistor [tolerance=±5% resistance=220 package=THT]
  R3 = Resistor [tolerance=±5% resistance=220 package=THT]
  R4 = Resistor [tolerance=±5% resistance=220 package=THT]
  R5 = Resistor [tolerance=±5% resistance=220 package=THT]
  R6 = Resistor [tolerance=±5% resistance=220 package=THT]
  R7 = Resistor [tolerance=±5% resistance=220 package=THT]
  R8 = Resistor [tolerance=±5% resistance=220 package=THT]
  R9 = Resistor [tolerance=±5% resistance=10k package=THT]

nets:
  GND: Part1.GND, U1.GND, U1.GND2
  N1: Part1.D10_PWM/SS, U1.LOAD
  N2: Part1.D11_PWM/MOSI, U1.CLK
  N3: Part1.D12/MISO, U1.DIN
  5V: Part1.5V, U1.VCC, R9.Pin_0
  N4: U1.SEGA, R2.Pin_1
  N5: U1.SEGF, R6.Pin_0
  N6: U1.SEGB, R3.Pin_1
  N7: U1.SEGG, R5.Pin_0
  N8: U1.ISET, R9.Pin_1
  N9: U1.SEGC, R4.Pin_1
  N10: U1.SEGE, R7.Pin_0
  N11: U1.SEGDP, R1.Pin_1
  N12: U1.SEGD, R8.Pin_0
